# Fritzing sketch UNO_flow_sensors (saved by Fritzing 0.9.3b)

parts:
  YF-S201_Flow_Meter1 = YF-S201 Water Flow Meter
  Part1 = Arduino Uno (Rev3)
  YF-S201_Flow_Meter2 = YF-S201 Water Flow Meter

nets:
  N1: YF-S201_Flow_Meter1.SIG, Part1.D2
  GND: YF-S201_Flow_Meter1.GND, Part1.GND, YF-S201_Flow_Meter2.GND
  VCC: YF-S201_Flow_Meter1.VCC, Part1.5V, YF-S201_Flow_Meter2.VCC
  N2: Part1.D3_PWM, YF-S201_Flow_Meter2.SIG

notes:
  Keep attaching sensors to D pins

custom parts:
  YF-S201 Water Flow Meter: The YF-S201 Flow Meter. The input voltage is 5V to 24V (DC).
