# Fritzing sketch pi_rfid_temp_pir (saved by Fritzing 0.9.3b)

parts:
  Raspberry_Pi_1 = Raspberry Pi 3 [part_number=RPI-3-V1.2]
  Part2 = RFID-RC522-v3
  PIR1 = PIR sensor
  DS1 = DS18B20 1-Wire Temperature Sensor [part_number=DS18B20]
  R1 = Resistor [tolerance=±5% resistance=4.7k package=THT]

nets:
  VDD: Raspberry_Pi_1.3v3, Part2.3.3V, PIR1.VDD, DS1.VDD, R1.Pin_1
  N1: Raspberry_Pi_1.GIPO4, DS1.DQ, R1.Pin_0
  GND: Raspberry_Pi_1.GIPO17, Raspberry_Pi_1.GIPO9, Raspberry_Pi_1.GND, Part2.MISO, Part2.GND, PIR1.SIG, PIR1.GND, DS1.GND
  N2: Raspberry_Pi_1.GIPO10, Raspberry_Pi_1.GIPO24, Part2.MOSI
  N3: Raspberry_Pi_1.GIPO11, Raspberry_Pi_1.GIPO7, Part2.SCK
  N4: Raspberry_Pi_1.GIPO8, Part2.SDA
  N5: Raspberry_Pi_1.GIPO25, Part2.RST

notes:
  GPIO4 (7)
  GPIO17 (11)
  GPIO8 (24)

custom parts:
  RFID-RC522-v3: A simple China made RFID-RC522 Reader (6x4 cm); do check the pin labels, as this is a MFRC522 based clone.
